# Fritzing sketch esp_pract (saved by Fritzing 0.9.4)
breadboards: 1

parts:
  U1 = NodeMCU V1.0
  R4 = Resistor [tolerance=±5% resistance=220 package=THT]
  7_Segment1 = 7 Segment Display  # not connected
  R2 = Resistor [tolerance=±5% resistance=1k package=THT]  # not connected
  S1 = Pushbutton [package="[THT]"]
  LED1 = LED - 5mm [color="Red (633nm)" package="5 mm [THT]"]  # not connected
  LED2 = LED - 5mm [color="Green (560nm)" package="5 mm [THT]"]
  LED3 = LED - 5mm [color="Yellow (595nm)" package="5 mm [THT]"]
  R5 = Resistor [tolerance=±5% resistance=220 package=THT]
  R6 = Resistor [tolerance=±5% resistance=220 package=THT]

nets:
  N1: U1.D2, LED3.anode
  N2: U1.D3, LED2.anode
  N3: U1.GND, R4.Pin_1, R5.Pin_1, R6.Pin_1
  N4: S1.Pin_1, S1.Pin_2
  N5: S1.Pin_3, S1.Pin_4
  N6: LED2.cathode, R6.Pin_0
  N7: LED3.cathode, R5.Pin_0

custom parts:
  NodeMCU V1.0: ESP8266 based NodeMCU
